# Fritzing sketch WiredButton (saved by Fritzing 0.9.3b)
breadboards: 1

parts:
  C1 = Electrolytic Capacitor [capacitance=1µF package="100 mil [THT, electrolytic]"]
  S2 = Pushbutton [package=THT]
  S1 = Pushbutton [package=THT]

nets:
  N1: C1.-, S1.leg1
  14V: C1.+, S2.leg1
  GND: S2.leg0, S1.leg0
