# Fritzing sketch bouncer (saved by Fritzing 0.9.3b)
circuit board: 5.65448cm x 7.17005cm
breadboards: 1

parts:
  hc-sr1 = hc-sr04
  R1 = Resistor [tolerance=±5% resistance=15k package=THT]
  R2 = Resistor [tolerance=±5% resistance=33k package=THT]
  OMRON1 = OMRON PCB Power Relay – G5LE [part_number="G5LE-1\n" package=THT]
  Q1 = NPN-Transistor [package="TO92 [THT]"]
  R3 = Resistor [tolerance=±5% resistance=1k package=THT]
  OMRON3 = OMRON PCB Power Relay – G5LE [part_number="G5LE-1\n" package=THT]
  Q3 = NPN-Transistor [package="TO92 [THT]"]
  R4 = Resistor [tolerance=±5% resistance=1k package=THT]
  J1 = Camdenboss CTB0158-2 [part_number=CTB0158-2 package=THT]
  Power_plug1 = Power plug
  R5 = Resistor [tolerance=±5% resistance=10k package=THT]
  C5 = Electrolytic Capacitor [capacitance=0.47mF package="100 mil [THT, electrolytic]"]
  C6 = Electrolytic Capacitor [capacitance=1µF package="100 mil [THT, electrolytic]"]
  C7 = Electrolytic Capacitor [capacitance=1µF package="100 mil [THT, electrolytic]"]
  Adafruit_HUZZAH_ESP8266_Breakout2 = Adafruit HUZZAH ESP8266 Breakout [part_number=2471]
  JP1 = Header 2 [package=molex-1x2_lock]

nets:
  VCC: hc-sr1.VCC, OMRON1.COIL2, OMRON3.COIL2, Power_plug1.VCC, R5.Pin_1, C5.+, C6.+, Adafruit_HUZZAH_ESP8266_Breakout2.V+
  N1: hc-sr1.Trig, Adafruit_HUZZAH_ESP8266_Breakout2.#4
  N2: hc-sr1.Echo, R2.Pin_0
  GND: hc-sr1.GND, R1.Pin_0, Q1.E, Q3.E, Power_plug1.GND, C5.-, C6.-, Adafruit_HUZZAH_ESP8266_Breakout2.GND, JP1.2
  N3: R1.Pin_1, R2.Pin_1, Adafruit_HUZZAH_ESP8266_Breakout2.#5
  N4: OMRON1.A, J1.pin2, C7.+
  N5: OMRON1.COIL1, Q1.B
  N6: OMRON1.C, OMRON3.C, J1.pin1
  N7: Q1.C, R3.Pin_0
  N8: R3.Pin_1, Adafruit_HUZZAH_ESP8266_Breakout2.#13
  N9: OMRON3.A, C7.-
  N10: OMRON3.COIL1, Q3.B
  N11: Q3.C, R4.Pin_0
  N12: R4.Pin_1, Adafruit_HUZZAH_ESP8266_Breakout2.#12
  N13: R5.Pin_0, Adafruit_HUZZAH_ESP8266_Breakout2.#14, JP1.1

notes:
  GND
  +5v
  R2
  R1
  R3
  R4
  R5
  C7
  C5
  C6
  Light
  Door
  Aidafruit HUZZAH ESP8266
  Bouncer v0
  HC-SR04
  BTN1

custom parts:
  Adafruit HUZZAH ESP8266 Breakout: The HUZZAH ESP8266 breakout is what we designed to make working with this chip super easy and a lot of fun. We took a certified module with an onboard antenna, and plenty of pins, and soldered it onto our designed breakout PCBs. We added in: Reset button, User button that can also put the chip into bootloading mode, Red LED you can blink Level shifting on the UART and reset pin 3.3V out, 500mA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
